// Logisim project CustomMultiplier.circ as structural Verilog: 1 circuit, main circuit CustomMultiplier
module CustomMultiplier (
  input  [7:0] FirstOperand,
  input  [7:0] SecondOperand,
  input  Clock,
  output [7:0] Result,
  output Done
);

  wire and_1_out, and_2_out, not_1_out;
  wire [7:0] counter_1_q, customadder_1_result;

  and and_1 (and_1_out, Clock, Done);
  Counter counter_1 (.load(1'b0), .up(1'b0), .clk(and_1_out), .Q(counter_1_q));  // open: clr, count, D, carry
  not not_1 (not_1_out, Done);
  and and_2 (and_2_out, not_1_out, Clock);
  CustomAdder customadder_1 (.FirstOperand(FirstOperand), .SecondOperand(Result), .Result(customadder_1_result));
  Register register_1 (.D(customadder_1_result), .clk(and_2_out), .Q(Result), .clr(1'b0));  // open: en
  Comparator comparator_1 (.a({8{1'b0}}), .b(counter_1_q), .eq(Done));  // open: gt, lt

  // Other names for the same wires on the sheet: A[7:0] = FirstOperand; B[7:0] = SecondOperand; clk = Clock;
  //   Res[7:0] = Result
endmodule
