// Logisim project ForCheck.circ as structural Verilog: 1 circuit, main circuit check
module check (
  input  clock,
  input  [7:0] value,
  output out_3
);


  assign out_3 = 1'b0;
endmodule
