// Logisim project MatrixCalculation.circ as structural Verilog: 1 circuit, main circuit MAC
module MAC (
  input  [31:0] A,
  input  [31:0] X,
  input  [31:0] B,
  input  clock,
  output [31:0] Result,
  output Done
);

  wire custommultiplier_1_done, custommultiplier_2_done, custommultiplier_3_done, custommultiplier_4_done,
       custommultiplier_5_done, custommultiplier_7_done, custommultiplier_8_p4;
  wire [7:0] customadder_1_result, customadder_2_result, customadder_3_result, customadder_4_p3,
       custommultiplier_1_result, custommultiplier_2_result, custommultiplier_3_result,
       custommultiplier_4_result, custommultiplier_5_result, custommultiplier_6_result,
       custommultiplier_7_result, custommultiplier_8_p3;

  CustomMultiplier custommultiplier_1 (
    .FirstOperand(A[7:0]), .SecondOperand(X[15:8]), .Result(custommultiplier_1_result),
    .Done(custommultiplier_1_done));  // open: Clock
  CustomMultiplier custommultiplier_2 (
    .FirstOperand(A[15:8]), .SecondOperand(X[31:24]), .Result(custommultiplier_2_result),
    .Done(custommultiplier_2_done));  // open: Clock
  CustomMultiplier custommultiplier_3 (
    .FirstOperand(A[23:16]), .SecondOperand(X[15:8]), .Clock(clock), .Result(custommultiplier_3_result),
    .Done(custommultiplier_3_done));
  CustomMultiplier custommultiplier_4 (
    .FirstOperand(A[31:24]), .SecondOperand(X[31:24]), .Clock(clock), .Result(custommultiplier_4_result),
    .Done(custommultiplier_4_done));
  CustomMultiplier custommultiplier_5 (
    .FirstOperand(A[7:0]), .SecondOperand(X[7:0]), .Result(custommultiplier_5_result),
    .Done(custommultiplier_5_done));  // open: Clock
  CustomMultiplier custommultiplier_6 (
    .FirstOperand(A[15:8]), .SecondOperand(X[23:16]), .Result(custommultiplier_6_result),
    .Done(custommultiplier_2_done));  // open: Clock
  CustomMultiplier custommultiplier_7 (
    .FirstOperand(A[23:16]), .SecondOperand(X[7:0]), .Result(custommultiplier_7_result),
    .Done(custommultiplier_7_done));  // open: Clock
  // CustomMultiplier custommultiplier_8: pin names not known; wires that end beside it: A[31:24], X[23:16], custommultiplier_8_p3, custommultiplier_8_p4
  CustomAdder customadder_1 (
    .FirstOperand(custommultiplier_5_result), .SecondOperand(custommultiplier_6_result),
    .Result(customadder_1_result));
  CustomAdder customadder_2 (
    .FirstOperand(custommultiplier_1_result), .SecondOperand(custommultiplier_2_result),
    .Result(customadder_2_result));
  CustomAdder customadder_3 (
    .FirstOperand(custommultiplier_7_result), .SecondOperand(custommultiplier_8_p3),
    .Result(customadder_3_result));
  // CustomAdder customadder_4: pin names not known; wires that end beside it: custommultiplier_4_result, custommultiplier_3_result, customadder_4_p3
  CustomAdder customadder_5 (.FirstOperand(customadder_2_result), .SecondOperand(B[15:8]), .Result(Result[15:8]));
  CustomAdder customadder_6 (.FirstOperand(customadder_4_p3), .SecondOperand(B[31:24]), .Result(Result[31:24]));
  CustomAdder customadder_7 (.FirstOperand(customadder_1_result), .SecondOperand(B[7:0]), .Result(Result[7:0]));
  CustomAdder customadder_8 (.FirstOperand(customadder_3_result), .SecondOperand(B[23:16]), .Result(Result[23:16]));
  and and_1 (Done, custommultiplier_5_done, custommultiplier_5_done, custommultiplier_1_done, custommultiplier_2_done, custommultiplier_4_done, custommultiplier_8_p4, custommultiplier_3_done, custommultiplier_7_done);

  // Other names for the same wires on the sheet: A_1_1[7:0] = A[7:0]; A_1_2[7:0] = A[15:8]; A_2_1[7:0] = A[23:16];
  //   A_2_2[7:0] = A[31:24]; B_1_1[7:0] = B[7:0]; B_1_2[7:0] = B[15:8]; B_2_1[7:0] = B[23:16]; B_2_2[7:0] = B[31:24];
  //   clk = clock; Result_1_1[7:0] = Result[7:0]; Result_1_2[7:0] = Result[15:8]; Result_2_1[7:0] = Result[23:16];
  //   Result_2_2[7:0] = Result[31:24]; X_1_1[7:0] = X[7:0]; X_1_2[7:0] = X[15:8]; X_2_1[7:0] = X[23:16];
  //   X_2_2[7:0] = X[31:24]

  // Notes on the sheet:
  //   Please don't change places of inputs and outputs
endmodule
